# Fritzing sketch solenoid (saved by Fritzing 0.9.3b)
breadboards: 1

parts:
  D1 = Rectifier Diode [part_number=1N4001 package="300 mil [THT]"]
  Q1 = NPN-Transistor [package="TO92 [THT]"]
  Part1 = Arduino Uno (Rev3)
  L1 = Solenoid

nets:
  N1: D1.cathode, Part1.5V, L1.pin2
  N2: D1.anode, Q1.C, L1.pin1
  N3: Q1.E, Part1.GND
  N4: Q1.B, Part1.D7

// code stored in the sketch: solenoid.ino
int solenoid = 4;

void setup() {
  // put your setup code here, to run once:
  pinMode(solenoid,OUTPUT);
  pinMode(LED_BUILTIN, OUTPUT);
}

void loop() {
  // put your main code here, to run repeatedly:
  digitalWrite(solenoid, HIGH);
  digitalWrite(LED_BUILTIN, HIGH);
  delay(2000);
  digitalWrite(solenoid, LOW);
  digitalWrite(LED_BUILTIN, LOW);
  delay(2000);
}
